// Logisim project ALU_template.circ as structural Verilog: 22 circuits, main circuit ALU32
module LeftShift32 (
  input  [31:0] B,
  input  [4:0] Sa,
  input  Cin,
  output [31:0] C
);

  wire [31:0] leftshift1_1_c, leftshift2_1_c, leftshift4_1_c, leftshift8_1_c, leftshift16_1_c,
       multiplexer_1_out, multiplexer_2_out, multiplexer_3_out, multiplexer_4_out;

  LeftShift1 leftshift1_1 (.Cin(Cin), .B(B), .C(leftshift1_1_c));
  Multiplexer #(.width(32), .enable("false")) multiplexer_1 (
    .in0(B), .in1(leftshift1_1_c), .out(multiplexer_1_out), .sel(Sa[0]));
  LeftShift2 leftshift2_1 (.Cin(Cin), .B(multiplexer_1_out), .C(leftshift2_1_c));
  Multiplexer #(.width(32), .enable("false")) multiplexer_2 (
    .in0(multiplexer_1_out), .in1(leftshift2_1_c), .out(multiplexer_2_out), .sel(Sa[1]));
  LeftShift4 leftshift4_1 (.Cin(Cin), .B(multiplexer_2_out), .C(leftshift4_1_c));
  Multiplexer #(.width(32), .enable("false")) multiplexer_3 (
    .in0(multiplexer_2_out), .in1(leftshift4_1_c), .out(multiplexer_3_out), .sel(Sa[2]));
  LeftShift8 leftshift8_1 (.Cin(Cin), .B(multiplexer_3_out), .C(leftshift8_1_c));
  Multiplexer #(.width(32), .enable("false")) multiplexer_4 (
    .in0(multiplexer_3_out), .in1(leftshift8_1_c), .out(multiplexer_4_out), .sel(Sa[3]));
  LeftShift16 leftshift16_1 (.Cin(Cin), .B(multiplexer_4_out), .C(leftshift16_1_c));
  Multiplexer #(.width(32), .enable("false")) multiplexer_5 (
    .in0(multiplexer_4_out), .in1(leftshift16_1_c), .out(C), .sel(Sa[4]));
endmodule

module Add32 (
  input  Cin,
  input  [31:0] B,
  input  [31:0] A,
  output [31:0] C,
  output V
);

  wire add1_1_cout, add1_2_cout, add1_3_cout, add1_4_cout, add1_5_cout, add1_6_cout, add1_7_cout,
       add1_8_cout, add1_9_cout, add1_10_cout, add1_11_cout, add1_12_cout, add1_13_cout, add1_14_cout,
       add1_15_cout, add1_16_cout, add1_17_cout, add1_18_cout, add1_19_cout, add1_20_cout, add1_21_cout,
       add1_22_cout, add1_23_cout, add1_24_cout, add1_25_cout, add1_26_cout, add1_27_cout, add1_28_cout,
       add1_29_cout, add1_30_cout, add1_31_cout, add1_32_cout;

  Add1 add1_1 (.A(A[0]), .B(B[0]), .Cin(Cin), .C(C[0]), .Cout(add1_1_cout));
  Add1 add1_2 (.A(A[1]), .B(B[1]), .Cin(add1_1_cout), .C(C[1]), .Cout(add1_2_cout));
  Add1 add1_3 (.A(A[2]), .B(B[2]), .Cin(add1_2_cout), .C(C[2]), .Cout(add1_3_cout));
  Add1 add1_4 (.A(A[3]), .B(B[3]), .Cin(add1_3_cout), .C(C[3]), .Cout(add1_4_cout));
  Add1 add1_5 (.A(A[4]), .B(B[4]), .Cin(add1_4_cout), .C(C[4]), .Cout(add1_5_cout));
  Add1 add1_6 (.A(A[5]), .B(B[5]), .Cin(add1_5_cout), .C(C[5]), .Cout(add1_6_cout));
  Add1 add1_7 (.A(A[6]), .B(B[6]), .Cin(add1_6_cout), .C(C[6]), .Cout(add1_7_cout));
  Add1 add1_8 (.A(A[7]), .B(B[7]), .Cin(add1_7_cout), .C(C[7]), .Cout(add1_8_cout));
  Add1 add1_9 (.A(A[8]), .B(B[8]), .Cin(add1_8_cout), .C(C[8]), .Cout(add1_9_cout));
  Add1 add1_10 (.A(A[9]), .B(B[9]), .Cin(add1_9_cout), .C(C[9]), .Cout(add1_10_cout));
  Add1 add1_11 (.A(A[10]), .B(B[10]), .Cin(add1_10_cout), .C(C[10]), .Cout(add1_11_cout));
  Add1 add1_12 (.A(A[11]), .B(B[11]), .Cin(add1_11_cout), .C(C[11]), .Cout(add1_12_cout));
  Add1 add1_13 (.A(A[12]), .B(B[12]), .Cin(add1_12_cout), .C(C[12]), .Cout(add1_13_cout));
  Add1 add1_14 (.A(A[13]), .B(B[13]), .Cin(add1_13_cout), .C(C[13]), .Cout(add1_14_cout));
  Add1 add1_15 (.A(A[14]), .B(B[14]), .Cin(add1_14_cout), .C(C[14]), .Cout(add1_15_cout));
  Add1 add1_16 (.A(A[15]), .B(B[15]), .Cin(add1_15_cout), .C(C[15]), .Cout(add1_16_cout));
  Add1 add1_17 (.A(A[16]), .B(B[16]), .Cin(add1_16_cout), .C(C[16]), .Cout(add1_17_cout));
  Add1 add1_18 (.A(A[17]), .B(B[17]), .Cin(add1_17_cout), .C(C[17]), .Cout(add1_18_cout));
  Add1 add1_19 (.A(A[18]), .B(B[18]), .Cin(add1_18_cout), .C(C[18]), .Cout(add1_19_cout));
  Add1 add1_20 (.A(A[19]), .B(B[19]), .Cin(add1_19_cout), .C(C[19]), .Cout(add1_20_cout));
  Add1 add1_21 (.A(A[20]), .B(B[20]), .Cin(add1_20_cout), .C(C[20]), .Cout(add1_21_cout));
  Add1 add1_22 (.A(A[21]), .B(B[21]), .Cin(add1_21_cout), .C(C[21]), .Cout(add1_22_cout));
  Add1 add1_23 (.A(A[22]), .B(B[22]), .Cin(add1_22_cout), .C(C[22]), .Cout(add1_23_cout));
  Add1 add1_24 (.A(A[23]), .B(B[23]), .Cin(add1_23_cout), .C(C[23]), .Cout(add1_24_cout));
  Add1 add1_25 (.A(A[24]), .B(B[24]), .Cin(add1_24_cout), .C(C[24]), .Cout(add1_25_cout));
  Add1 add1_26 (.A(A[25]), .B(B[25]), .Cin(add1_25_cout), .C(C[25]), .Cout(add1_26_cout));
  Add1 add1_27 (.A(A[26]), .B(B[26]), .Cin(add1_26_cout), .C(C[26]), .Cout(add1_27_cout));
  Add1 add1_28 (.A(A[27]), .B(B[27]), .Cin(add1_27_cout), .C(C[27]), .Cout(add1_28_cout));
  Add1 add1_29 (.A(A[28]), .B(B[28]), .Cin(add1_28_cout), .C(C[28]), .Cout(add1_29_cout));
  Add1 add1_30 (.A(A[29]), .B(B[29]), .Cin(add1_29_cout), .C(C[29]), .Cout(add1_30_cout));
  Add1 add1_31 (.A(A[30]), .B(B[30]), .Cin(add1_30_cout), .C(C[30]), .Cout(add1_31_cout));
  Add1 add1_32 (.A(A[31]), .B(B[31]), .Cin(add1_31_cout), .C(C[31]), .Cout(add1_32_cout));
  xor xor_1 (V, add1_31_cout, add1_32_cout);
endmodule

module LeftShift1 (
  input  Cin,
  input  [31:0] B,
  output [31:0] C
);


  assign C = {B[30:0], Cin};
endmodule

module LeftShift2 (
  input  Cin,
  input  [31:0] B,
  output [31:0] C
);

  wire [31:0] leftshift1_1_c;

  LeftShift1 leftshift1_1 (.Cin(Cin), .B(B), .C(leftshift1_1_c));
  LeftShift1 leftshift1_2 (.Cin(Cin), .B(leftshift1_1_c), .C(C));
endmodule

module LeftShift4 (
  input  Cin,
  input  [31:0] B,
  output [31:0] C
);

  wire [31:0] leftshift2_1_c;

  LeftShift2 leftshift2_1 (.Cin(Cin), .B(B), .C(leftshift2_1_c));
  LeftShift2 leftshift2_2 (.Cin(Cin), .B(leftshift2_1_c), .C(C));
endmodule

module LeftShift8 (
  input  Cin,
  input  [31:0] B,
  output [31:0] C
);

  wire [31:0] leftshift4_1_c;

  LeftShift4 leftshift4_1 (.Cin(Cin), .B(B), .C(leftshift4_1_c));
  LeftShift4 leftshift4_2 (.Cin(Cin), .B(leftshift4_1_c), .C(C));
endmodule

module LeftShift16 (
  input  Cin,
  input  [31:0] B,
  output [31:0] C
);

  wire [31:0] leftshift8_1_c;

  LeftShift8 leftshift8_1 (.Cin(Cin), .B(B), .C(leftshift8_1_c));
  LeftShift8 leftshift8_2 (.Cin(Cin), .B(leftshift8_1_c), .C(C));
endmodule

module Add1 (
  input  A,
  input  B,
  input  Cin,
  output C,
  output Cout
);

  wire and_1_out, and_2_out, xor_1_out;

  xor xor_1 (xor_1_out, A, B);
  and and_1 (and_1_out, A, B);
  and and_2 (and_2_out, Cin, xor_1_out);
  xor xor_2 (C, xor_1_out, Cin);
  or or_1 (Cout, and_1_out, and_2_out);
endmodule

module Sub32 (
  input  Bin,
  input  [31:0] B,
  input  [31:0] A,
  output [31:0] C,
  output V
);

  wire [31:0] negator_1_out;

  Negator #(.width(32)) negator_1 (.in(B), .out(negator_1_out));
  Add32 add32_1 (.Cin(Bin), .B(negator_1_out), .A(A), .C(C), .V(V));
endmodule

module ALU32 (
  input  [31:0] A,
  input  [31:0] B,
  input  [4:0] Sa,
  input  [3:0] Op,
  output V,
  output [31:0] C
);

  wire a_b_comparator_1_v, a_b_logic_1_v, add_sub_1_v, shiftlr_1_v;
  wire [31:0] a_b_comparator_1_c, a_b_logic_1_c, add_sub_1_c, shiftlr_1_c;

  A_B_Logic a_b_logic_1 (.A(A), .B(B), .Op(Op), .V(a_b_logic_1_v), .C(a_b_logic_1_c));
  Add_Sub add_sub_1 (.B(B), .A(A), .Op(Op), .C(add_sub_1_c), .V(add_sub_1_v));
  ShiftLR shiftlr_1 (.Sa(Sa), .B(B), .Op(Op), .C(shiftlr_1_c), .V(shiftlr_1_v));
  A_B_Comparator a_b_comparator_1 (.B(B), .A(A), .Op(Op), .V(a_b_comparator_1_v), .C(a_b_comparator_1_c));
  or or_1 (V, a_b_logic_1_v, add_sub_1_v, shiftlr_1_v, a_b_comparator_1_v);
  assign C = a_b_logic_1_c | add_sub_1_c | shiftlr_1_c | a_b_comparator_1_c;  // OR_Gate or_2, 32 bits wide
endmodule

module Add_Sub (
  input  [31:0] B,
  input  [31:0] A,
  input  [3:0] Op,
  output [31:0] C,
  output V
);

  wire add32_1_v, and_1_out, and_4_out, not_1_out, not_2_out, not_3_out, or_3_out;
  wire [31:0] add32_1_c, and_2_out, and_3_out, negate_1_minusa, or_1_out, or_2_out, signedextend_1to32_1_xt,
       signedextend_1to32_2_xt;

  Negate negate_1 (.A(B), .minusA(negate_1_minusa));
  SignedExtend_1to32 signedextend_1to32_1 (.t(and_1_out), .Xt(signedextend_1to32_1_xt));
  and and_1 (and_1_out, not_1_out, Op[2], Op[1]);
  not not_1 (not_1_out, Op[3]);
  assign and_2_out = negate_1_minusa & signedextend_1to32_1_xt;  // AND_Gate and_2, 32 bits wide
  assign and_3_out = B & signedextend_1to32_2_xt;  // AND_Gate and_3, 32 bits wide
  SignedExtend_1to32 signedextend_1to32_2 (.t(and_4_out), .Xt(signedextend_1to32_2_xt));
  and and_4 (and_4_out, not_3_out, not_2_out, Op[1]);
  not not_2 (not_2_out, Op[2]);
  not not_3 (not_3_out, Op[3]);
  assign or_1_out = and_2_out | and_3_out;  // OR_Gate or_1, 32 bits wide
  Add32 add32_1 (.Cin(1'b0), .B(or_1_out), .A(A), .C(add32_1_c), .V(add32_1_v));
  assign or_2_out = signedextend_1to32_1_xt | signedextend_1to32_2_xt;  // OR_Gate or_2, 32 bits wide
  or or_3 (or_3_out, and_1_out, and_4_out);
  and and_5 (V, add32_1_v, or_3_out);
  assign C = add32_1_c & or_2_out;  // AND_Gate and_6, 32 bits wide

  // Notes on the sheet:
  //   (1)
  //   (2)
endmodule

module ShiftLR (
  input  [4:0] Sa,
  input  [31:0] B,
  input  [3:0] Op,
  output [31:0] C,
  output V
);

  wire and_1_out, and_3_out, and_5_out, and_6_out, msb_1_msb_b, not_1_out, not_2_out, not_3_out, not_4_out,
       not_5_out, not_6_out, or_1_out;
  wire [31:0] and_2_out, and_4_out, and_7_out, and_8_out, leftshift32_1_c, or_2_out, reverse_1_a_rev,
       reverse_2_a_rev, signedextend_1to32_1_xt, signedextend_1to32_2_xt;

  MSB msb_1 (.B(B), .MSB_B(msb_1_msb_b));
  not not_1 (not_1_out, Op[3]);
  SignedExtend_1to32 signedextend_1to32_1 (.t(and_1_out), .Xt(signedextend_1to32_1_xt));
  and and_1 (and_1_out, not_1_out, not_2_out, not_3_out);
  not not_2 (not_2_out, Op[2]);
  not not_3 (not_3_out, Op[1]);
  assign and_2_out = B & signedextend_1to32_1_xt;  // AND_Gate and_2, 32 bits wide
  and and_3 (and_3_out, Op[3], Op[2], not_4_out, not_5_out);
  Reverse reverse_1 (.A(B), .A_rev(reverse_1_a_rev));
  SignedExtend_1to32 signedextend_1to32_2 (.t(or_1_out), .Xt(signedextend_1to32_2_xt));
  or or_1 (or_1_out, and_3_out, and_5_out);
  not not_4 (not_4_out, Op[1]);
  not not_5 (not_5_out, Op[0]);
  assign and_4_out = reverse_1_a_rev & signedextend_1to32_2_xt;  // AND_Gate and_4, 32 bits wide
  and and_5 (and_5_out, Op[3], Op[2], not_6_out, Op[0]);
  not not_6 (not_6_out, Op[1]);
  assign or_2_out = and_2_out | and_4_out;  // OR_Gate or_2, 32 bits wide
  and and_6 (and_6_out, msb_1_msb_b, and_5_out);
  LeftShift32 leftshift32_1 (.B(or_2_out), .Sa(Sa), .Cin(and_6_out), .C(leftshift32_1_c));
  Reverse reverse_2 (.A(leftshift32_1_c), .A_rev(reverse_2_a_rev));
  assign and_7_out = signedextend_1to32_2_xt & reverse_2_a_rev;  // AND_Gate and_7, 32 bits wide
  assign and_8_out = signedextend_1to32_1_xt & leftshift32_1_c;  // AND_Gate and_8, 32 bits wide
  assign C = and_7_out | and_8_out;  // OR_Gate or_3, 32 bits wide

  assign V = 1'b0;
endmodule

module Reverse (
  input  [31:0] A,
  output [31:0] A_rev
);


  assign A_rev = {A[0], A[1], A[2], A[3], A[4], A[5], A[6], A[7], A[8], A[9], A[10], A[11], A[12], A[13], A[14], A[15], A[16], A[17], A[18], A[19], A[20], A[21], A[22], A[23], A[24], A[25], A[26], A[27], A[28], A[29], A[30], A[31]};
endmodule

module MSB (
  input  [31:0] B,
  output MSB_B
);


  assign MSB_B = B[31];
endmodule

module A_B_Comparator (
  input  [31:0] B,
  input  [31:0] A,
  input  [3:0] Op,
  output V,
  output [31:0] C
);

  wire and_1_out, and_2_out, and_3_out, and_4_out, and_5_out, and_6_out, and_7_out, and_8_out,
       isequal_1_aisequalb, islezero_1_le, not_1_out, not_2_out, not_3_out, not_4_out, not_5_out, not_6_out,
       not_7_out, not_8_out, or_1_out;

  IsEqual isequal_1 (.B(B), .A(A), .AisequalB(isequal_1_aisequalb));
  IsLEZero islezero_1 (.A(A), .LE(islezero_1_le));
  not not_1 (not_1_out, islezero_1_le);
  not not_2 (not_2_out, isequal_1_aisequalb);
  and and_1 (and_1_out, Op[3], not_3_out, not_5_out, not_4_out);
  not not_3 (not_3_out, Op[2]);
  not not_4 (not_4_out, Op[0]);
  not not_5 (not_5_out, Op[1]);
  and and_2 (and_2_out, not_2_out, and_1_out);
  and and_3 (and_3_out, Op[3], not_6_out, not_7_out, Op[0]);
  not not_6 (not_6_out, Op[2]);
  not not_7 (not_7_out, Op[1]);
  and and_4 (and_4_out, isequal_1_aisequalb, and_3_out);
  and and_5 (and_5_out, islezero_1_le, and_6_out);
  and and_6 (and_6_out, Op[3], Op[2], Op[1], not_8_out);
  not not_8 (not_8_out, Op[0]);
  and and_7 (and_7_out, Op[3], Op[2], Op[1], Op[0]);
  and and_8 (and_8_out, not_1_out, and_7_out);
  or or_1 (or_1_out, and_4_out, and_2_out, and_5_out, and_8_out);
  ZeroExtend_1to32 zeroextend_1to32_1 (.in_1(or_1_out), .out_2(C));

  assign V = 1'b0;
endmodule

module IsZero (
  input  [31:0] A,
  output Is_Zero
);

  wire not_1_out, not_2_out, not_3_out, not_4_out, not_5_out, not_6_out, not_7_out, not_8_out, not_9_out,
       not_10_out, not_11_out, not_12_out, not_13_out, not_14_out, not_15_out, not_16_out, not_17_out,
       not_18_out, not_19_out, not_20_out, not_21_out, not_22_out, not_23_out, not_24_out, not_25_out,
       not_26_out, not_27_out, not_28_out, not_29_out, not_30_out, not_31_out, not_32_out;

  not not_1 (not_1_out, A[0]);
  not not_2 (not_2_out, A[1]);
  not not_3 (not_3_out, A[2]);
  not not_4 (not_4_out, A[3]);
  not not_5 (not_5_out, A[4]);
  not not_6 (not_6_out, A[5]);
  not not_7 (not_7_out, A[6]);
  not not_8 (not_8_out, A[7]);
  not not_9 (not_9_out, A[8]);
  not not_10 (not_10_out, A[9]);
  not not_11 (not_11_out, A[10]);
  not not_12 (not_12_out, A[11]);
  not not_13 (not_13_out, A[12]);
  not not_14 (not_14_out, A[13]);
  not not_15 (not_15_out, A[14]);
  not not_16 (not_16_out, A[15]);
  not not_17 (not_17_out, A[16]);
  not not_18 (not_18_out, A[17]);
  not not_19 (not_19_out, A[18]);
  not not_20 (not_20_out, A[19]);
  not not_21 (not_21_out, A[20]);
  not not_22 (not_22_out, A[21]);
  not not_23 (not_23_out, A[22]);
  not not_24 (not_24_out, A[23]);
  not not_25 (not_25_out, A[24]);
  not not_26 (not_26_out, A[25]);
  not not_27 (not_27_out, A[26]);
  not not_28 (not_28_out, A[27]);
  not not_29 (not_29_out, A[28]);
  not not_30 (not_30_out, A[29]);
  not not_31 (not_31_out, A[30]);
  not not_32 (not_32_out, A[31]);
  and and_1 (Is_Zero, not_1_out, not_2_out, not_3_out, not_4_out, not_5_out, not_6_out, not_7_out, not_8_out, not_9_out, not_10_out, not_11_out, not_12_out, not_13_out, not_14_out, not_15_out, not_16_out, not_17_out, not_18_out, not_19_out, not_20_out, not_21_out, not_22_out, not_23_out, not_24_out, not_25_out, not_26_out, not_27_out, not_28_out, not_29_out, not_30_out, not_31_out, not_32_out);
endmodule

module IsLEZero (
  input  [31:0] A,
  output LE
);

  wire iszero_1_is_zero, msb_1_msb_b;

  MSB msb_1 (.B(A), .MSB_B(msb_1_msb_b));
  IsZero iszero_1 (.A(A), .Is_Zero(iszero_1_is_zero));
  or or_1 (LE, msb_1_msb_b, iszero_1_is_zero);
endmodule

module A_B_Logic (
  input  [31:0] A,
  input  [31:0] B,
  input  [3:0] Op,
  output V,
  output [31:0] C
);

  wire and_2_out, and_5_out, and_7_out, and_8_out, not_1_out, not_2_out, not_3_out, not_4_out, not_5_out,
       not_6_out, not_7_out, not_8_out;
  wire [31:0] and_1_out, and_3_out, and_4_out, and_6_out, and_9_out, nor_1_out, or_1_out,
       signedextend_1to32_1_xt, signedextend_1to32_2_xt, signedextend_1to32_3_xt, signedextend_1to32_4_xt,
       xor_1_out;

  assign and_1_out = A & B;  // AND_Gate and_1, 32 bits wide
  SignedExtend_1to32 signedextend_1to32_1 (.t(and_2_out), .Xt(signedextend_1to32_1_xt));
  and and_2 (and_2_out, not_2_out, Op[2], not_1_out, not_3_out);
  not not_1 (not_1_out, Op[1]);
  not not_2 (not_2_out, Op[3]);
  assign or_1_out = A | B;  // OR_Gate or_1, 32 bits wide
  assign and_3_out = and_1_out & signedextend_1to32_1_xt;  // AND_Gate and_3, 32 bits wide
  not not_3 (not_3_out, Op[0]);
  assign and_4_out = or_1_out & signedextend_1to32_2_xt;  // AND_Gate and_4, 32 bits wide
  SignedExtend_1to32 signedextend_1to32_2 (.t(and_5_out), .Xt(signedextend_1to32_2_xt));
  and and_5 (and_5_out, not_4_out, Op[2], not_5_out, Op[0]);
  not not_4 (not_4_out, Op[3]);
  not not_5 (not_5_out, Op[1]);
  assign xor_1_out = A ^ B;  // XOR_Gate xor_1, 32 bits wide
  assign and_6_out = xor_1_out & signedextend_1to32_3_xt;  // AND_Gate and_6, 32 bits wide
  SignedExtend_1to32 signedextend_1to32_3 (.t(and_7_out), .Xt(signedextend_1to32_3_xt));
  and and_7 (and_7_out, Op[3], not_7_out, Op[1], not_6_out);
  not not_6 (not_6_out, Op[0]);
  not not_7 (not_7_out, Op[2]);
  assign nor_1_out = ~(A | B);  // NOR_Gate nor_1, 32 bits wide
  SignedExtend_1to32 signedextend_1to32_4 (.t(and_8_out), .Xt(signedextend_1to32_4_xt));
  and and_8 (and_8_out, Op[3], not_8_out, Op[1], Op[0]);
  not not_8 (not_8_out, Op[2]);
  assign and_9_out = nor_1_out & signedextend_1to32_4_xt;  // AND_Gate and_9, 32 bits wide
  assign C = and_3_out | and_4_out | and_6_out | and_9_out;  // OR_Gate or_2, 32 bits wide

  assign V = 1'b0;

  // Notes on the sheet:
  //   (i)
  //   (1)
  //   (2)
  //   (ii)
  //   (3)
  //   (iii)
  //   (iv)
  //   (4)
  //   (5)
endmodule

module IsEqual (
  input  [31:0] B,
  input  [31:0] A,
  output AisequalB
);

  wire [31:0] add32_1_c, negate_1_minusa;

  Negate negate_1 (.A(B), .minusA(negate_1_minusa));
  Add32 add32_1 (.Cin(1'b0), .B(negate_1_minusa), .A(A), .C(add32_1_c));  // open: V
  IsZero iszero_1 (.A(add32_1_c), .Is_Zero(AisequalB));
endmodule

module SignedExtend_1to32 (
  input  t,
  output [31:0] Xt
);


  assign Xt = {32{t}};
endmodule

module Negate (
  input  [31:0] A,
  output [31:0] minusA
);

  wire [31:0] not_1_out;

  not not_1 (not_1_out[0], A[0]);
  not not_2 (not_1_out[1], A[1]);
  not not_3 (not_1_out[2], A[2]);
  not not_4 (not_1_out[3], A[3]);
  not not_5 (not_1_out[4], A[4]);
  not not_6 (not_1_out[5], A[5]);
  not not_7 (not_1_out[6], A[6]);
  not not_8 (not_1_out[7], A[7]);
  not not_9 (not_1_out[8], A[8]);
  not not_10 (not_1_out[9], A[9]);
  not not_11 (not_1_out[10], A[10]);
  not not_12 (not_1_out[11], A[11]);
  not not_13 (not_1_out[12], A[12]);
  not not_14 (not_1_out[13], A[13]);
  not not_15 (not_1_out[14], A[14]);
  not not_16 (not_1_out[15], A[15]);
  not not_17 (not_1_out[16], A[16]);
  not not_18 (not_1_out[17], A[17]);
  not not_19 (not_1_out[18], A[18]);
  not not_20 (not_1_out[19], A[19]);
  not not_21 (not_1_out[20], A[20]);
  not not_22 (not_1_out[21], A[21]);
  not not_23 (not_1_out[22], A[22]);
  not not_24 (not_1_out[23], A[23]);
  not not_25 (not_1_out[24], A[24]);
  not not_26 (not_1_out[25], A[25]);
  not not_27 (not_1_out[26], A[26]);
  not not_28 (not_1_out[27], A[27]);
  not not_29 (not_1_out[28], A[28]);
  not not_30 (not_1_out[29], A[29]);
  not not_31 (not_1_out[30], A[30]);
  not not_32 (not_1_out[31], A[31]);
  Add32 add32_1 (.Cin(1'b0), .B(32'h1), .A(not_1_out), .C(minusA));  // open: V
endmodule

module ZeroExtend_1to32 (
  input  in_1,
  output [31:0] out_2
);


  assign out_2 = {{31{1'b0}}, in_1};
endmodule
